# Fritzing sketch BuddyBot2_Fritzing (saved by Fritzing 0.9.2b)
circuit board: 5.95896cm x 5.01555cm

parts:
  Part1 = Arduino Micro (Rev3)
  LED1 = smd LED [color="Red (633nm)" package="0805 [SMD]"]
  Part2 = Bluetooth HC-05 Macho
  J2 = Basic Servo
  J3 = Basic Servo

nets:
  GND: Part1.GND, LED1.cathode, Part2.GND, J2.gnd, J3.gnd
  N1: Part1.D5_PWM, J2.pulse
  N2: Part1.D6_PWM/A7, J3.pulse
  N3: Part1.D7, LED1.anode
  N4: Part1.D10_PWM/A10, Part2.TXD
  N5: Part1.D11_PWM, Part2.RXD
  VCC: Part1.5V, Part2.VCC, J2.vcc, J3.vcc

// code stored in the sketch: BuddyBot2_Fritzing.ino

